// Logisim project booth_logisim_evolution.circ as structural Verilog: 1 circuit, main circuit main
module main (
  input  [3:0] M,
  input  [8:0] in_2,
  input  start,
  output [8:0] out_4
);

  wire clk_out, reset_out;
  wire [3:0] adder_1_out, multiplexer_1_out, multiplexer_2_out, subtractor_1_out;
  wire [8:0] multiplexer_2_out_2, multiplexer_3_out, multiplexer_4_out, shifter_1_out;

  // Probe on M
  Clock clk (.out(clk_out));
  Button reset (.out(reset_out));
  // Probe on multiplexer_1_out
  Multiplexer #(.width(4)) multiplexer_1 (
    .in0(in_2[4:1]), .in1(multiplexer_2_out), .out(multiplexer_1_out), .sel(start));
  Multiplexer #(.width(9)) multiplexer_2 (
    .in0(in_2), .in1(out_4), .out({multiplexer_2_out_2[8:5], multiplexer_2_out, multiplexer_2_out_2[0]}),
    .sel(start));
  Adder #(.width(4)) adder_1 (.a(M), .b(multiplexer_2_out_2[8:5]), .out(adder_1_out));  // open: cin, cout
  Subtractor #(.width(4)) subtractor_1 (
    .a(multiplexer_2_out_2[8:5]), .b(M), .out(subtractor_1_out));  // open: bin, bout
  Multiplexer #(.width(9)) multiplexer_3 (
    .in0({multiplexer_2_out_2[8:5], multiplexer_2_out, multiplexer_2_out_2[0]}), .in1(shifter_1_out),
    .out(multiplexer_3_out), .sel(start));
  Multiplexer #(.select(2), .width(9)) multiplexer_4 (
    .in0(out_4), .in1({adder_1_out, multiplexer_1_out, multiplexer_2_out_2[0]}),
    .in2({subtractor_1_out, multiplexer_1_out, multiplexer_2_out_2[0]}), .in3(out_4),
    .out(multiplexer_4_out), .sel(out_4[1:0]));
  Register #(.width(9)) register_1 (.D(multiplexer_3_out), .en(1'b1), .clk(clk_out), .Q(out_4), .clr(reset_out));
  // Probe on out_4[1:0]
  Shifter #(.shift("ar"), .width(9)) shifter_1 (.in(multiplexer_4_out), .\dist (4'b0001), .out(shifter_1_out));
  // Probe on out_4

  // Notes on the sheet:
  //   AQQ-1
  //   A
  //   Q-1
  //   A+M
  //   A-M
endmodule
