// Logisim project project0_2_1.circ as structural Verilog: 1 circuit, main circuit main
module main (
  input  A,
  input  D,
  input  EN,
  input  enable,
  input  B,
  input  EN_2,
  input  D_2,
  output out_8,
  output A0,
  output out_10,
  output A1,
  output A3,
  output out_13,
  output A4
);

  wire adder_1_cout, adder_1_out, adder_2_cout, adder_2_out, adder_3_cout, adder_3_out, adder_4_out,
       button_1_out, clk_out, clock_1_out, multiplexer_1_out, not_2_out, not_3_out, transmission_1_p3;

  Clock clk (.out(clk_out));
  // Transmission_Gate transmission_1: pin names not known; wires that end beside it: A, EN, transmission_1_p3, out_10
  not not_1 (transmission_1_p3, EN);
  // Transmission_Gate transmission_2: pin names not known; wires that end beside it: B, transmission_1_p3, EN, out_10
  Multiplexer multiplexer_1 (.in0(multiplexer_1_out), .in1(D_2), .out(multiplexer_1_out), .sel(clk_out));
  not not_2 (not_2_out, clk_out);
  Multiplexer multiplexer_2 (.in0(out_13), .in1(multiplexer_1_out), .out(out_13), .sel(not_2_out));
  Multiplexer multiplexer_3 (.in0(out_8), .in1(D), .out(out_8), .sel(EN_2));
  not not_3 (not_3_out, enable);
  Adder #(.width(1)) adder_1 (.a(A0), .b(not_3_out), .out(adder_1_out), .cin(enable), .cout(adder_1_cout));
  Adder #(.width(1)) adder_2 (.a(A1), .b(adder_1_cout), .out(adder_2_out), .cin(enable), .cout(adder_2_cout));
  Adder #(.width(1)) adder_3 (.a(A3), .b(adder_2_cout), .out(adder_3_out), .cin(enable), .cout(adder_3_cout));
  Adder #(.width(1)) adder_4 (.a(A4), .b(adder_3_cout), .out(adder_4_out), .cin(enable));  // open: cout
  D_Flip_Flop d_ff_1 (.D(adder_1_out), .clk(clock_1_out), .Q(A0), .reset(button_1_out));  // open: Qn, preset
  D_Flip_Flop d_ff_2 (.D(adder_2_out), .clk(clock_1_out), .Q(A1), .reset(button_1_out));  // open: Qn, preset
  D_Flip_Flop d_ff_3 (.D(adder_3_out), .clk(clock_1_out), .Q(A3), .reset(button_1_out));  // open: Qn, preset
  D_Flip_Flop d_ff_4 (.D(adder_4_out), .clk(clock_1_out), .Q(A4), .reset(button_1_out));  // open: Qn, preset
  Clock clock_1 (.out(clock_1_out));
  Button button_1 (.out(button_1_out));

  // Notes on the sheet:
  //   MUX using Transmission gates
  //   D-FF using Latches
  //   master
  //   slave
  //   Latch using MUXs
  //   Synchronous Up/Down counter using D-FF and adder
  //   clk
  //   reset
endmodule
